// Logisim project circuito_completo.circ as structural Verilog: 4 circuits, main circuit main
module main (
  input  in_1,
  input  in_2,
  input  in_3,
  input  in_4,
  input  in_5,
  input  in_6,
  input  in_7,
  input  in_8,
  input  in_9,
  input  in_10,
  input  in_11,
  input  in_12,
  input  in_13,
  input  in_14,
  input  in_15,
  input  in_16,
  input  in_17,
  input  in_18,
  input  in_19,
  input  in_20,
  input  in_21,
  input  in_22,
  input  in_23,
  input  in_24,
  input  in_25,
  input  in_26,
  input  in_27,
  input  in_28,
  input  in_29,
  input  in_30,
  input  in_31,
  input  in_32,
  input  in_33,
  input  in_34,
  input  in_35,
  input  in_36,
  input  in_37,
  input  in_38,
  input  in_39,
  input  in_40,
  input  in_41,
  output out_42,
  output out_43,
  output out_44,
  output out_45,
  output out_46,
  output out_47,
  output out_48,
  output out_49,
  output out_50
);

  wire integrado_2_cout, integrado_3_cout, integrado_4_cout, integrado_5_cout, integrado_6_cout,
       integrado_7_cout, integrado_8_cout;

  INTEGRADO integrado_1 (
    .A(in_33), .B(in_25), .C1(in_1), .C2(in_9), .C3(in_17), .Cin(integrado_2_cout), .S(out_43), .Cout(out_42));
  INTEGRADO integrado_2 (
    .A(in_34), .B(in_26), .C1(in_2), .C2(in_10), .C3(in_18), .Cin(integrado_3_cout), .S(out_44),
    .Cout(integrado_2_cout));
  INTEGRADO integrado_3 (
    .A(in_35), .B(in_27), .C1(in_3), .C2(in_11), .C3(in_19), .Cin(integrado_4_cout), .S(out_45),
    .Cout(integrado_3_cout));
  INTEGRADO integrado_4 (
    .A(in_36), .B(in_28), .C1(in_4), .C2(in_12), .C3(in_20), .Cin(integrado_5_cout), .S(out_46),
    .Cout(integrado_4_cout));
  INTEGRADO integrado_5 (
    .A(in_37), .B(in_29), .C1(in_5), .C2(in_13), .C3(in_21), .Cin(integrado_6_cout), .S(out_47),
    .Cout(integrado_5_cout));
  INTEGRADO integrado_6 (
    .A(in_38), .B(in_30), .C1(in_6), .C2(in_14), .C3(in_22), .Cin(integrado_7_cout), .S(out_48),
    .Cout(integrado_6_cout));
  INTEGRADO integrado_7 (
    .A(in_39), .B(in_31), .C1(in_7), .C2(in_15), .C3(in_23), .Cin(integrado_8_cout), .S(out_49),
    .Cout(integrado_7_cout));
  INTEGRADO integrado_8 (
    .A(in_40), .B(in_32), .C1(in_8), .C2(in_16), .C3(in_24), .Cin(in_41), .S(out_50), .Cout(integrado_8_cout));
endmodule

module decoder (
  input  A,
  input  B,
  input  C
);

  wire AND_out, NAND_out, NOR_out, not_1_out, not_2_out, not_3_out, NOT_4_out, OR_out, SOMADOR_out, XNOR_out,
       XOR_out;

  not not_1 (not_1_out, A);
  not not_2 (not_2_out, B);
  not not_3 (not_3_out, C);
  and AND (AND_out, not_1_out, not_2_out, not_3_out);
  and OR (OR_out, not_1_out, not_2_out, C);
  and NOT_4 (NOT_4_out, not_1_out, B, not_3_out);
  and NAND (NAND_out, not_1_out, B, C);
  and NOR (NOR_out, A, not_2_out, not_3_out);
  and XOR (XOR_out, A, not_2_out, C);
  and XNOR (XNOR_out, A, B, not_3_out);
  and SOMADOR (SOMADOR_out, C, B, A);

  // Notes on the sheet:
  //   B
  //   A
  //   C
endmodule

module \Unidade_Lógica  (
  input  A,
  input  B
);

  wire and_1_out, AND_2_out, nand_1_out, NAND_2_out, nor_1_out, NOR_2_out, not_1_out, NOT_2_out, or_1_out,
       OR_2_out, or_3_out, or_4_out, undriven, xnor_1_out, XNOR_2_out, xor_1_out, XOR_2_out;

  and and_1 (and_1_out, B, A);
  or or_1 (or_1_out, A, B);
  not not_1 (not_1_out, A);
  nand nand_1 (nand_1_out, A, B);
  nor nor_1 (nor_1_out, A, B);
  xor xor_1 (xor_1_out, A, B);
  xnor xnor_1 (xnor_1_out, A, B);
  buf AND_2 (AND_2_out, and_1_out);  // AND_Gate
  buf OR_2 (OR_2_out, or_1_out);  // AND_Gate
  buf NOT_2 (NOT_2_out, not_1_out);  // AND_Gate
  buf NAND_2 (NAND_2_out, nand_1_out);  // AND_Gate
  buf NOR_2 (NOR_2_out, nor_1_out);  // AND_Gate
  buf XOR_2 (XOR_2_out, xor_1_out);  // AND_Gate
  buf XNOR_2 (XNOR_2_out, xnor_1_out);  // AND_Gate
  or or_3 (or_3_out, AND_2_out, OR_2_out, NOT_2_out, NAND_2_out);
  or or_4 (or_4_out, NOR_2_out, XOR_2_out, XNOR_2_out, undriven);
  // OR_Gate or_5 has open pins: in1=or_3_out, in3=or_4_out, out=open
endmodule

module INTEGRADO (
  input  A,
  input  B,
  input  Cin,
  input  C1,
  input  C2,
  input  C3,
  output S,
  output Cout
);

  wire and_1_out, and_2_out, and_3_out, and_4_out, and_5_out, and_6_out, and_7_out, and_8_out, and_9_out,
       and_10_out, and_11_out, and_12_out, and_13_out, and_14_out, and_15_out, and_16_out, and_17_out,
       and_18_out, and_19_out, nand_1_out, nor_1_out, not_1_out, not_2_out, not_3_out, not_4_out, or_1_out,
       or_2_out, or_3_out, xnor_1_out, xor_1_out, xor_2_out, xor_3_out;

  not not_1 (not_1_out, C1);
  not not_2 (not_2_out, C2);
  not not_3 (not_3_out, C3);
  and and_1 (and_1_out, not_1_out, not_2_out, not_3_out);
  and and_2 (and_2_out, not_1_out, not_2_out, C3);
  and and_3 (and_3_out, not_1_out, C2, not_3_out);
  and and_4 (and_4_out, not_1_out, C2, C3);
  and and_5 (and_5_out, C1, not_2_out, not_3_out);
  and and_6 (and_6_out, C1, not_2_out, C3);
  and and_7 (and_7_out, C1, C2, not_3_out);
  and and_8 (and_8_out, C3, C2, C1);
  and and_9 (and_9_out, B, A);
  or or_1 (or_1_out, A, B);
  not not_4 (not_4_out, A);
  nand nand_1 (nand_1_out, A, B);
  nor nor_1 (nor_1_out, A, B);
  xor xor_1 (xor_1_out, A, B);
  xnor xnor_1 (xnor_1_out, A, B);
  and and_10 (and_10_out, and_9_out, and_1_out);
  and and_11 (and_11_out, or_1_out, and_2_out);
  and and_12 (and_12_out, not_4_out, and_3_out);
  and and_13 (and_13_out, nand_1_out, and_4_out);
  and and_14 (and_14_out, nor_1_out, and_5_out);
  and and_15 (and_15_out, xor_1_out, and_6_out);
  and and_16 (and_16_out, xnor_1_out, and_7_out);
  or or_2 (or_2_out, and_10_out, and_11_out, and_12_out, and_13_out);
  or or_3 (or_3_out, and_14_out, and_15_out, and_16_out);
  xor xor_2 (xor_2_out, B, A);
  and and_17 (and_17_out, and_8_out, A, B);
  xor xor_3 (xor_3_out, Cin, xor_2_out);
  and and_18 (and_18_out, xor_3_out, and_8_out);
  and and_19 (and_19_out, Cin, xor_2_out, and_8_out);
  or or_4 (S, or_2_out, or_3_out, and_18_out);
  or or_5 (Cout, and_19_out, and_17_out);
endmodule
